# Fritzing sketch pressure sensor LED (saved by Fritzing 0.9.3b)
breadboards: 1

parts:
  Part1 = Arduino Leonardo (Rev3b)
  R1 = Resistor [tolerance=±5% resistance=220 package="0805 [SMD]"]
  R2 = Resistor [tolerance=±5% resistance=220 package="0805 [SMD]"]
  J1 = Basic Force Sensing Resistor (FSR) [package=THT]
  LED1 = smd LED [color="Red (633nm)" package="0805 [SMD]"]

nets:
  N1: Part1.5V, J1.pin_0
  N2: Part1.GND, R1.Pin_0, R2.Pin_1, LED1.anode
  N3: Part1.A0, R2.Pin_0, J1.pin_1
  N4: R1.Pin_1, LED1.cathode
